// Logisim project control_logic.circ as structural Verilog: 1 circuit, main circuit control_logic
module control_logic (
  input  [31:0] inst,
  input  BrEq,
  input  BrLt,
  output PCSel,
  output RegWEn,
  output [2:0] ImmSel,
  output BrUn,
  output ASel,
  output BSel,
  output [3:0] ALUSel,
  output MemRW,
  output [1:0] WBSel,
  output CSRSel,
  output CSRWen
);

  wire and_1_out, and_2_out, and_3_out, and_4_out, and_5_out, comparator_11_eq, comparator_12_eq,
       comparator_13_eq, comparator_14_eq, comparator_15_eq, comparator_16_eq, is_auipc, is_B_type, is_CSR,
       is_I_type, is_J_type, is_jalr, is_load_inst, is_lui, is_R_type, is_S_type, is_U_type, not_1_out,
       not_2_out, or_1_out, or_2_out, or_3_out;
  wire [2:0] multiplexer_1_out, multiplexer_2_out, multiplexer_3_out, multiplexer_4_out;

  Comparator #(.width(7)) comparator_1 (.a(inst[6:0]), .b(7'b0110011), .eq(is_R_type));  // open: gt, lt
  Comparator #(.width(7)) comparator_2 (.a(inst[6:0]), .b(7'b0000011), .eq(is_load_inst));  // open: gt, lt
  Comparator #(.width(7)) comparator_3 (.a(inst[6:0]), .b(7'b0010011), .eq(is_I_type));  // open: gt, lt
  Comparator #(.width(7)) comparator_4 (.a(inst[6:0]), .b(7'b0100011), .eq(is_S_type));  // open: gt, lt
  Comparator #(.width(7)) comparator_5 (.a(inst[6:0]), .b(7'b1100011), .eq(is_B_type));  // open: gt, lt
  Comparator #(.width(7)) comparator_6 (.a(inst[6:0]), .b(7'b0010111), .eq(is_auipc));  // open: gt, lt
  Comparator #(.width(7)) comparator_7 (.a(inst[6:0]), .b(7'b0110111), .eq(is_lui));  // open: gt, lt
  Comparator #(.width(7)) comparator_8 (.a(inst[6:0]), .b(7'b1101111), .eq(is_J_type));  // open: gt, lt
  Comparator #(.width(7)) comparator_9 (.a(inst[6:0]), .b(7'b1100111), .eq(is_jalr));  // open: gt, lt
  Comparator #(.width(7)) comparator_10 (.a(inst[6:0]), .b(7'b1110011), .eq(is_CSR));  // open: gt, lt
  Comparator #(.width(3)) comparator_11 (.a(inst[14:12]), .b(3'b110), .eq(comparator_11_eq));  // open: gt, lt
  Comparator #(.width(3)) comparator_12 (.a(inst[14:12]), .b(3'b100), .eq(comparator_12_eq));  // open: gt, lt
  Comparator #(.width(3)) comparator_13 (.a(inst[14:12]), .b(3'b101), .eq(comparator_13_eq));  // open: gt, lt
  Comparator #(.width(3)) comparator_14 (.a(inst[14:12]), .b(3'b111), .eq(comparator_14_eq));  // open: gt, lt
  Multiplexer #(.enable("false"), .width(3)) multiplexer_1 (
    .in0(3'b000), .in1(3'b001), .out(multiplexer_1_out), .sel(is_S_type));
  Comparator #(.width(3)) comparator_15 (.a(inst[14:12]), .b(3'b000), .eq(comparator_15_eq));  // open: gt, lt
  Comparator #(.width(3)) comparator_16 (.a(inst[14:12]), .b(3'b001), .eq(comparator_16_eq));  // open: gt, lt
  not not_1 (not_1_out, BrEq);
  or or_1 (or_1_out, comparator_11_eq, comparator_12_eq);
  or or_2 (or_2_out, comparator_13_eq, comparator_14_eq);
  not not_2 (not_2_out, BrLt);
  Multiplexer #(.enable("false"), .width(3)) multiplexer_2 (
    .in0(multiplexer_1_out), .in1(3'b010), .out(multiplexer_2_out), .sel(is_B_type));
  and and_1 (and_1_out, comparator_15_eq, BrEq);
  and and_2 (and_2_out, comparator_16_eq, not_1_out);
  and and_3 (and_3_out, or_1_out, BrLt);
  and and_4 (and_4_out, or_2_out, not_2_out);
  Multiplexer #(.enable("false"), .width(3)) multiplexer_3 (
    .in0(multiplexer_2_out), .in1(3'b011), .out(multiplexer_3_out), .sel(is_U_type));
  or or_3 (or_3_out, and_1_out, and_2_out, and_3_out, and_4_out);
  Multiplexer #(.enable("false"), .width(3)) multiplexer_4 (
    .in0(multiplexer_3_out), .in1(3'b100), .out(multiplexer_4_out), .sel(is_J_type));
  or or_4 (is_U_type, is_auipc, is_lui);
  Multiplexer #(.enable("false"), .width(3)) multiplexer_5 (
    .in0(multiplexer_4_out), .in1(3'b101), .out(ImmSel), .sel(is_CSR));
  and and_5 (and_5_out, is_B_type, or_3_out);
  or or_5 (PCSel, is_J_type, and_5_out, is_jalr);
  or or_6 (RegWEn, is_R_type, is_I_type, is_auipc, is_lui, is_J_type, is_jalr);

  assign ALUSel = 4'b0000;
  assign ASel = 1'b0;
  assign BSel = 1'b1;
  assign MemRW = 1'b0;
  assign WBSel = 2'b01;

  // Other names for the same wires on the sheet: immediate_type[2:0] = ImmSel; opcode[6:0] = inst[6:0];
  //   rd[4:0] = inst[11:7]; funct3[2:0] = inst[14:12]; rs1[4:0] = inst[19:15]; rs2[4:0] = inst[24:20];
  //   funct7[6:0] = inst[31:25]; is_jal = is_J_type; should_branch = PCSel; should_write_back_reg = RegWEn

  // Notes on the sheet:
  //   INPUTS to your circuit
  //   DON'T CHANGE THE LOCATIONS OF THE INPUTS AND OUTPUTS!
  //   OUTPUT from your circuit
endmodule
